// Digital circuit Subterranean2.0.dig as structural Verilog
module Subterranean2_0 (
  input  [63:0] _0_63_2,
  input  _256_2,
  input  [63:0] _64_127_2,
  input  [63:0] _128_191_2,
  input  [63:0] _191_255_2,
  output [63:0] _0_63,
  output [63:0] _64_127,
  output [63:0] _128_191,
  output [63:0] _191_255,
  output _256
);

  wire \θ_1_p1 , \θ_1_p2 , \θ_1_p8 , \θ_1_p13 , \ι_1_o256 , \χ_1_p6 , \χ_1_p7 , \χ_1_p13 ;
  wire [63:0] \θ_1_p9 , \θ_1_p10 , \θ_1_p11 , \θ_1_p12 , \ι_1_o0_63 , \ι_1_o64_127 , \ι_1_o128_191 ,
       \ι_1_o192_255 , \χ_1_p9 , \χ_1_p10 , \χ_1_p11 , \χ_1_p12 ;

  // χ χ_1: pin names not known; wires that end beside it: _0_63_2, _64_127_2, _128_191_2, _191_255_2, _256_2, \χ_1_p6 , \χ_1_p7 , \χ_1_p6 , \χ_1_p9 , \χ_1_p10 , \χ_1_p11 , \χ_1_p12 , \χ_1_p13 
  \ι  \u_ι_1  (
    ._64_127(\χ_1_p9 ), ._128_191(\χ_1_p10 ), ._191_255(\χ_1_p11 ), ._0_63(\χ_1_p12 ), ._256(\χ_1_p13 ),
    .o0_63(\ι_1_o0_63 ), .o64_127(\ι_1_o64_127 ), .o128_191(\ι_1_o128_191 ), .o192_255(\ι_1_o192_255 ),
    .o256(\ι_1_o256 ));
  // θ θ_1: pin names not known; wires that end beside it: \θ_1_p1 , \θ_1_p2 , \ι_1_o0_63 , \ι_1_o64_127 , \ι_1_o128_191 , \ι_1_o192_255 , \ι_1_o256 , \θ_1_p8 , \θ_1_p9 , \θ_1_p10 , \θ_1_p11 , \θ_1_p12 , \θ_1_p13 
  \π  \u_π_1  (
    ._64_127(\θ_1_p9 ), ._128_191(\θ_1_p10 ), ._191_255(\θ_1_p11 ), ._0_63(\θ_1_p12 ), ._256(\θ_1_p13 ),
    .o0_63(_0_63), .o64_127(_64_127), .o128_191(_128_191), .o192_255(_191_255), .o256(_256));
endmodule
