// Digital circuit subterranean_absorb_keyed.dig as structural Verilog
module subterranean_absorb_keyed (
  input  [63:0] State_in_0_63,
  input  [63:0] State_in_128_191,
  input  [63:0] State_in_192_255,
  input  [63:0] State_in_64_127,
  input  State_in_256,
  input  [63:0] value_in_0_63,
  input  [63:0] value_in_64_127,
  output [63:0] State__0_63,
  output [63:0] State__64_127,
  output [63:0] State__128_191,
  output [63:0] State__192_255,
  output State__256
);

  wire subterranean_duplex_1_state__256, subterranean_duplex_2_state__256, subterranean_duplex_3_state__256;
  wire [1:1] subterranean_duplex_4_state__0_63;
  wire [63:0] subterranean_duplex_1_state__0_63, subterranean_duplex_1_state__64_127,
       subterranean_duplex_1_state__128_191, subterranean_duplex_1_state__192_255,
       subterranean_duplex_2_state__0_63, subterranean_duplex_2_state__64_127,
       subterranean_duplex_2_state__128_191, subterranean_duplex_2_state__192_255,
       subterranean_duplex_3_state__0_63, subterranean_duplex_3_state__64_127,
       subterranean_duplex_3_state__128_191, subterranean_duplex_3_state__192_255;

  subterranean_duplex subterranean_duplex_1 (
    .state_0_63(State_in_0_63), .state_128_191(State_in_64_127), .state_192_255(State_in_128_191),
    .state_64_127(State_in_192_255), .state_256(State_in_256), .sigma(value_in_0_63[31:0]),
    .state__0_63(subterranean_duplex_1_state__0_63), .state__64_127(subterranean_duplex_1_state__64_127),
    .state__128_191(subterranean_duplex_1_state__128_191),
    .state__192_255(subterranean_duplex_1_state__192_255), .state__256(subterranean_duplex_1_state__256));
  subterranean_duplex subterranean_duplex_2 (
    .state_0_63(subterranean_duplex_1_state__0_63), .state_128_191(subterranean_duplex_1_state__64_127),
    .state_192_255(subterranean_duplex_1_state__128_191),
    .state_64_127(subterranean_duplex_1_state__192_255), .state_256(subterranean_duplex_1_state__256),
    .sigma(value_in_0_63[63:32]), .state__0_63(subterranean_duplex_2_state__0_63),
    .state__64_127(subterranean_duplex_2_state__64_127),
    .state__128_191(subterranean_duplex_2_state__128_191),
    .state__192_255(subterranean_duplex_2_state__192_255), .state__256(subterranean_duplex_2_state__256));
  subterranean_duplex subterranean_duplex_3 (
    .state_0_63(subterranean_duplex_2_state__0_63), .state_128_191(subterranean_duplex_2_state__64_127),
    .state_192_255(subterranean_duplex_2_state__128_191),
    .state_64_127(subterranean_duplex_2_state__192_255), .state_256(subterranean_duplex_2_state__256),
    .sigma(value_in_64_127[31:0]), .state__0_63(subterranean_duplex_3_state__0_63),
    .state__64_127(subterranean_duplex_3_state__64_127),
    .state__128_191(subterranean_duplex_3_state__128_191),
    .state__192_255(subterranean_duplex_3_state__192_255), .state__256(subterranean_duplex_3_state__256));
  subterranean_duplex subterranean_duplex_4 (
    .state_0_63(subterranean_duplex_3_state__0_63), .state_128_191(subterranean_duplex_3_state__64_127),
    .state_192_255(subterranean_duplex_3_state__128_191),
    .state_64_127(subterranean_duplex_3_state__192_255), .state_256(subterranean_duplex_3_state__256),
    .sigma(value_in_64_127[63:32]),
    .state__0_63({State__0_63[63:2], subterranean_duplex_4_state__0_63[1], State__0_63[0]}),
    .state__64_127(State__64_127), .state__128_191(State__128_191), .state__192_255(State__192_255),
    .state__256(State__256));
  xor xor_1 (State__0_63[1], 1'b1, subterranean_duplex_4_state__0_63[1]);

  // Notes on the sheet:
  //   This is an inlined duplex_0bit
endmodule

/* Test case:
State_in_{0-63} State_in_{128-191} State_in_{192-255} State_in_{64-127} State_in_{256} value-in_{0-63} value-in_{64-127} State'_{0-63} State'_{64-127} State'_{128-191} State'_{192-255} State'_256
0x0 0x0 0x0 0x0 0 0x0 0x0 0x6168ffeb39984b7 0x92583e62104b7b31 0x4f1a43be51a8dc 0x93ceb1620ee96237 1
0x6 0x0 0x0 0x0 0 0x0 0x0 0xe3a866b635c62363 0xca26df7d89b1e1e2 0xdd389318c34e21cf 0x3eb0cc777445462c 0
*/
