// Digital circuit subterranean_duplex_0bit.dig as structural Verilog
module subterranean_duplex_0bit (
  input  [63:0] state_0_63,
  input  [63:0] state_128_191,
  input  [63:0] state_192_255,
  input  [63:0] state_64_127,
  input  state_256,
  output [63:0] D0State__0_63,
  output [63:0] D0State__64_127,
  output [63:0] D0State__128_191,
  output [63:0] D0State__192_255,
  output D0State__256
);

  wire [1:1] subterranean_round_1_o0_63;

  Subterranean_round subterranean_round_1 (
    ._0_63(state_0_63), ._64_127(state_64_127), ._128_191(state_128_191), ._192_255(state_192_255),
    ._256(state_256), .o0_63({D0State__0_63[63:2], subterranean_round_1_o0_63[1], D0State__0_63[0]}),
    .o64_127(D0State__64_127), .o128_191(D0State__128_191), .o191_255(D0State__192_255), .o256(D0State__256));
  xor xor_1 (D0State__0_63[1], 1'b1, subterranean_round_1_o0_63[1]);
endmodule
