// Digital circuit subterranean_round.dig as structural Verilog
module subterranean_round (
  input  [63:0] _0_63,
  input  [63:0] _64_127,
  input  [63:0] _128_191,
  input  [63:0] _192_255,
  input  _256,
  output [63:0] o0_63,
  output [63:0] o64_127,
  output [63:0] o128_191,
  output [63:0] o191_255,
  output o256
);

  wire chi_1_o256, i_1_o256, thetha_1_o256;
  wire [63:0] chi_1_o0_63, chi_1_o64_127, chi_1_o128_191, chi_1_o192_255, i_1_o0_63, i_1_o64_127,
       i_1_o128_191, i_1_o192_255, thetha_1_o0_63, thetha_1_o64_127, thetha_1_o128_191, thetha_1_o192_255;

  chi chi_1 (
    ._64_127(_0_63), ._128_191(_64_127), ._191_255(_128_191), ._0_63(_192_255), ._256(_256),
    .o0_63(chi_1_o0_63), .o64_127(chi_1_o64_127), .o128_191(chi_1_o128_191), .o192_255(chi_1_o192_255),
    .o256(chi_1_o256));
  i i_1 (
    ._64_127(chi_1_o0_63), ._128_191(chi_1_o64_127), ._191_255(chi_1_o128_191), ._0_63(chi_1_o192_255),
    ._256(chi_1_o256), .o0_63(i_1_o0_63), .o64_127(i_1_o64_127), .o128_191(i_1_o128_191),
    .o192_255(i_1_o192_255), .o256(i_1_o256));
  thetha thetha_1 (
    ._0_63(i_1_o0_63), ._64_127(i_1_o64_127), ._128_191(i_1_o128_191), ._192_255(i_1_o192_255),
    ._256(i_1_o256), .o0_63(thetha_1_o0_63), .o64_127(thetha_1_o64_127), .o128_191(thetha_1_o128_191),
    .o192_255(thetha_1_o192_255), .o256(thetha_1_o256));
  pi pi_1 (
    ._64_127(thetha_1_o0_63), ._128_191(thetha_1_o64_127), ._191_255(thetha_1_o128_191),
    ._0_63(thetha_1_o192_255), ._256(thetha_1_o256), .o0_63(o0_63), .o64_127(o64_127), .o128_191(o128_191),
    .o192_255(o191_255), .o256(o256));
endmodule
