// Digital circuit x.dig as structural Verilog
// x1 of chi
module x (
  input  [2:0] s,
  output o
);

  wire and_1_out, xor_1_out;

  xor xor_1 (xor_1_out, s[1], 1'b1);
  and and_1 (and_1_out, xor_1_out, s[2]);
  xor xor_2 (o, s[0], and_1_out);
endmodule
