// Digital circuit x64-61.dig as structural Verilog
// x64 of chi
module x64_61 (
  input  [63:0] i_64,
  output [61:0] o_64
);

  x x_1 (.s(i_64[2:0]), .o(o_64[0]));
  x x_2 (.s(i_64[3:1]), .o(o_64[1]));
  x x_3 (.s(i_64[4:2]), .o(o_64[2]));
  x x_4 (.s(i_64[5:3]), .o(o_64[3]));
  x x_5 (.s(i_64[6:4]), .o(o_64[4]));
  x x_6 (.s(i_64[7:5]), .o(o_64[5]));
  x x_7 (.s(i_64[8:6]), .o(o_64[6]));
  x x_8 (.s(i_64[9:7]), .o(o_64[7]));
  x x_9 (.s(i_64[10:8]), .o(o_64[8]));
  x x_10 (.s(i_64[11:9]), .o(o_64[9]));
  x x_11 (.s(i_64[12:10]), .o(o_64[10]));
  x x_12 (.s(i_64[13:11]), .o(o_64[11]));
  x x_13 (.s(i_64[14:12]), .o(o_64[12]));
  x x_14 (.s(i_64[15:13]), .o(o_64[13]));
  x x_15 (.s(i_64[16:14]), .o(o_64[14]));
  x x_16 (.s(i_64[17:15]), .o(o_64[15]));
  x x_17 (.s(i_64[18:16]), .o(o_64[16]));
  x x_18 (.s(i_64[19:17]), .o(o_64[17]));
  x x_19 (.s(i_64[20:18]), .o(o_64[18]));
  x x_20 (.s(i_64[21:19]), .o(o_64[19]));
  x x_21 (.s(i_64[22:20]), .o(o_64[20]));
  x x_22 (.s(i_64[23:21]), .o(o_64[21]));
  x x_23 (.s(i_64[24:22]), .o(o_64[22]));
  x x_24 (.s(i_64[25:23]), .o(o_64[23]));
  x x_25 (.s(i_64[26:24]), .o(o_64[24]));
  x x_26 (.s(i_64[27:25]), .o(o_64[25]));
  x x_27 (.s(i_64[28:26]), .o(o_64[26]));
  x x_28 (.s(i_64[29:27]), .o(o_64[27]));
  x x_29 (.s(i_64[30:28]), .o(o_64[28]));
  x x_30 (.s(i_64[31:29]), .o(o_64[29]));
  x x_31 (.s(i_64[32:30]), .o(o_64[30]));
  x x_32 (.s(i_64[33:31]), .o(o_64[31]));
  x x_33 (.s(i_64[34:32]), .o(o_64[32]));
  x x_34 (.s(i_64[35:33]), .o(o_64[33]));
  x x_35 (.s(i_64[36:34]), .o(o_64[34]));
  x x_36 (.s(i_64[37:35]), .o(o_64[35]));
  x x_37 (.s(i_64[38:36]), .o(o_64[36]));
  x x_38 (.s(i_64[39:37]), .o(o_64[37]));
  x x_39 (.s(i_64[40:38]), .o(o_64[38]));
  x x_40 (.s(i_64[41:39]), .o(o_64[39]));
  x x_41 (.s(i_64[42:40]), .o(o_64[40]));
  x x_42 (.s(i_64[43:41]), .o(o_64[41]));
  x x_43 (.s(i_64[44:42]), .o(o_64[42]));
  x x_44 (.s(i_64[45:43]), .o(o_64[43]));
  x x_45 (.s(i_64[46:44]), .o(o_64[44]));
  x x_46 (.s(i_64[47:45]), .o(o_64[45]));
  x x_47 (.s(i_64[48:46]), .o(o_64[46]));
  x x_48 (.s(i_64[49:47]), .o(o_64[47]));
  x x_49 (.s(i_64[50:48]), .o(o_64[48]));
  x x_50 (.s(i_64[51:49]), .o(o_64[49]));
  x x_51 (.s(i_64[52:50]), .o(o_64[50]));
  x x_52 (.s(i_64[53:51]), .o(o_64[51]));
  x x_53 (.s(i_64[54:52]), .o(o_64[52]));
  x x_54 (.s(i_64[55:53]), .o(o_64[53]));
  x x_55 (.s(i_64[56:54]), .o(o_64[54]));
  x x_56 (.s(i_64[57:55]), .o(o_64[55]));
  x x_57 (.s(i_64[58:56]), .o(o_64[56]));
  x x_58 (.s(i_64[59:57]), .o(o_64[57]));
  x x_59 (.s(i_64[60:58]), .o(o_64[58]));
  x x_60 (.s(i_64[61:59]), .o(o_64[59]));
  x x_61 (.s(i_64[62:60]), .o(o_64[60]));
  x x_62 (.s(i_64[63:61]), .o(o_64[61]));
endmodule
