// Digital circuit ι.dig as structural Verilog
// ι : si ← si + δi
// where δ_i = 1 if i = 0 else 1
module \ι  (
  input  [63:0] _64_127,
  input  [63:0] _128_191,
  input  [63:0] _191_255,
  input  [63:0] _0_63,
  input  _256,
  output [63:0] _0_63_2,
  output [63:0] _64_127_2,
  output [63:0] _128_191_2,
  output [63:0] _192_255,
  output _256_2
);

  xor xor_1 (_0_63_2[0], _0_63[0], 1'b1);

  assign _0_63_2[63:1] = _0_63[63:1];
  assign _64_127_2 = _64_127;
  assign _128_191_2 = _128_191;
  assign _192_255 = _191_255;
  assign _256_2 = _256;
endmodule
