// Digital circuit ι64-56.dig as structural Verilog
module \ι64_56  (
  input  [63:0] _0_63,
  output [55:0] _0_55
);

  xor xor_1 (_0_55[0], _0_63[0], _0_63[3], _0_63[8]);
  xor xor_2 (_0_55[1], _0_63[1], _0_63[4], _0_63[9]);
  xor xor_3 (_0_55[2], _0_63[2], _0_63[5], _0_63[10]);
  xor xor_4 (_0_55[3], _0_63[3], _0_63[6], _0_63[11]);
  xor xor_5 (_0_55[4], _0_63[4], _0_63[7], _0_63[12]);
  xor xor_6 (_0_55[5], _0_63[5], _0_63[8], _0_63[13]);
  xor xor_7 (_0_55[6], _0_63[6], _0_63[9], _0_63[14]);
  xor xor_8 (_0_55[7], _0_63[7], _0_63[10], _0_63[15]);
  xor xor_9 (_0_55[8], _0_63[8], _0_63[11], _0_63[16]);
  xor xor_10 (_0_55[9], _0_63[9], _0_63[12], _0_63[17]);
  xor xor_11 (_0_55[10], _0_63[10], _0_63[13], _0_63[18]);
  xor xor_12 (_0_55[11], _0_63[11], _0_63[14], _0_63[19]);
  xor xor_13 (_0_55[12], _0_63[12], _0_63[15], _0_63[20]);
  xor xor_14 (_0_55[13], _0_63[13], _0_63[16], _0_63[21]);
  xor xor_15 (_0_55[14], _0_63[14], _0_63[17], _0_63[22]);
  xor xor_16 (_0_55[15], _0_63[15], _0_63[18], _0_63[23]);
  xor xor_17 (_0_55[16], _0_63[16], _0_63[19], _0_63[24]);
  xor xor_18 (_0_55[17], _0_63[17], _0_63[20], _0_63[25]);
  xor xor_19 (_0_55[18], _0_63[18], _0_63[21], _0_63[26]);
  xor xor_20 (_0_55[19], _0_63[19], _0_63[22], _0_63[27]);
  xor xor_21 (_0_55[20], _0_63[20], _0_63[23], _0_63[28]);
  xor xor_22 (_0_55[21], _0_63[21], _0_63[24], _0_63[29]);
  xor xor_23 (_0_55[22], _0_63[22], _0_63[25], _0_63[30]);
  xor xor_24 (_0_55[23], _0_63[23], _0_63[26], _0_63[31]);
  xor xor_25 (_0_55[24], _0_63[24], _0_63[27], _0_63[32]);
  xor xor_26 (_0_55[25], _0_63[25], _0_63[28], _0_63[33]);
  xor xor_27 (_0_55[26], _0_63[26], _0_63[29], _0_63[34]);
  xor xor_28 (_0_55[27], _0_63[27], _0_63[30], _0_63[35]);
  xor xor_29 (_0_55[28], _0_63[28], _0_63[31], _0_63[36]);
  xor xor_30 (_0_55[29], _0_63[29], _0_63[32], _0_63[37]);
  xor xor_31 (_0_55[30], _0_63[30], _0_63[33], _0_63[38]);
  xor xor_32 (_0_55[31], _0_63[31], _0_63[34], _0_63[39]);
  xor xor_33 (_0_55[32], _0_63[32], _0_63[35], _0_63[40]);
  xor xor_34 (_0_55[33], _0_63[33], _0_63[36], _0_63[41]);
  xor xor_35 (_0_55[34], _0_63[34], _0_63[37], _0_63[42]);
  xor xor_36 (_0_55[35], _0_63[35], _0_63[38], _0_63[43]);
  xor xor_37 (_0_55[36], _0_63[36], _0_63[39], _0_63[44]);
  xor xor_38 (_0_55[37], _0_63[37], _0_63[40], _0_63[45]);
  xor xor_39 (_0_55[38], _0_63[38], _0_63[41], _0_63[46]);
  xor xor_40 (_0_55[39], _0_63[39], _0_63[42], _0_63[47]);
  xor xor_41 (_0_55[40], _0_63[40], _0_63[43], _0_63[48]);
  xor xor_42 (_0_55[41], _0_63[41], _0_63[44], _0_63[49]);
  xor xor_43 (_0_55[42], _0_63[42], _0_63[45], _0_63[50]);
  xor xor_44 (_0_55[43], _0_63[43], _0_63[46], _0_63[51]);
  xor xor_45 (_0_55[44], _0_63[44], _0_63[47], _0_63[52]);
  xor xor_46 (_0_55[45], _0_63[45], _0_63[48], _0_63[53]);
  xor xor_47 (_0_55[46], _0_63[46], _0_63[49], _0_63[54]);
  xor xor_48 (_0_55[47], _0_63[47], _0_63[50], _0_63[55]);
  xor xor_49 (_0_55[48], _0_63[48], _0_63[51], _0_63[56]);
  xor xor_50 (_0_55[49], _0_63[49], _0_63[52], _0_63[57]);
  xor xor_51 (_0_55[50], _0_63[50], _0_63[53], _0_63[58]);
  xor xor_52 (_0_55[51], _0_63[51], _0_63[54], _0_63[59]);
  xor xor_53 (_0_55[52], _0_63[52], _0_63[55], _0_63[60]);
  xor xor_54 (_0_55[53], _0_63[53], _0_63[56], _0_63[61]);
  xor xor_55 (_0_55[54], _0_63[54], _0_63[57], _0_63[62]);
  xor xor_56 (_0_55[55], _0_63[55], _0_63[58], _0_63[63]);
endmodule
