// Digital circuit π.dig as structural Verilog
// π : s_i ← s_12i
module \π  (
  input  [63:0] _64_127,
  input  [63:0] _128_191,
  input  [63:0] _191_255,
  input  [63:0] _0_63,
  input  _256,
  output [63:0] _0_63_2,
  output [63:0] _64_127_2,
  output [63:0] _128_191_2,
  output [63:0] _192_255,
  output _256_2
);


  assign _0_63_2 = {_191_255[50], _191_255[38], _191_255[26], _191_255[14], _191_255[2], _128_191[54], _128_191[42], _128_191[30], _128_191[18], _128_191[6], _64_127[58], _64_127[46], _64_127[34], _64_127[22], _64_127[10], _0_63[62], _0_63[50], _0_63[38], _0_63[26], _0_63[14], _0_63[2], _191_255[55], _191_255[43], _191_255[31], _191_255[19], _191_255[7], _128_191[59], _128_191[47], _128_191[35], _128_191[23], _128_191[11], _64_127[63], _64_127[51], _64_127[39], _64_127[27], _64_127[15], _64_127[3], _0_63[55], _0_63[43], _0_63[31], _0_63[19], _0_63[7], _191_255[60], _191_255[48], _191_255[36], _191_255[24], _191_255[12], _191_255[0], _128_191[52], _128_191[40], _128_191[28], _128_191[16], _128_191[4], _64_127[56], _64_127[44], _64_127[32], _64_127[20], _64_127[8], _0_63[60], _0_63[48], _0_63[36], _0_63[24], _0_63[12], _0_63[0]};
  assign _64_127_2 = {_191_255[47], _191_255[35], _191_255[23], _191_255[11], _128_191[63], _128_191[51], _128_191[39], _128_191[27], _128_191[15], _128_191[3], _64_127[55], _64_127[43], _64_127[31], _64_127[19], _64_127[7], _0_63[59], _0_63[47], _0_63[35], _0_63[23], _0_63[11], _256, _191_255[52], _191_255[40], _191_255[28], _191_255[16], _191_255[4], _128_191[56], _128_191[44], _128_191[32], _128_191[20], _128_191[8], _64_127[60], _64_127[48], _64_127[36], _64_127[24], _64_127[12], _64_127[0], _0_63[52], _0_63[40], _0_63[28], _0_63[16], _0_63[4], _191_255[57], _191_255[45], _191_255[33], _191_255[21], _191_255[9], _128_191[61], _128_191[49], _128_191[37], _128_191[25], _128_191[13], _128_191[1], _64_127[53], _64_127[41], _64_127[29], _64_127[17], _64_127[5], _0_63[57], _0_63[45], _0_63[33], _0_63[21], _0_63[9], _191_255[62]};
  assign _128_191_2 = {_191_255[41], _191_255[29], _191_255[17], _191_255[5], _128_191[57], _128_191[45], _128_191[33], _128_191[21], _128_191[9], _64_127[61], _64_127[49], _64_127[37], _64_127[25], _64_127[13], _64_127[1], _0_63[53], _0_63[41], _0_63[29], _0_63[17], _0_63[5], _191_255[58], _191_255[46], _191_255[34], _191_255[22], _191_255[10], _128_191[62], _128_191[50], _128_191[38], _128_191[26], _128_191[14], _128_191[2], _64_127[54], _64_127[42], _64_127[30], _64_127[18], _64_127[6], _0_63[58], _0_63[46], _0_63[34], _0_63[22], _0_63[10], _191_255[63], _191_255[51], _191_255[39], _191_255[27], _191_255[15], _191_255[3], _128_191[55], _128_191[43], _128_191[31], _128_191[19], _128_191[7], _64_127[59], _64_127[47], _64_127[35], _64_127[23], _64_127[11], _0_63[63], _0_63[51], _0_63[39], _0_63[27], _0_63[15], _0_63[3], _191_255[56]};
  assign _192_255 = {_191_255[44], _191_255[32], _191_255[20], _191_255[8], _128_191[60], _128_191[48], _128_191[36], _128_191[24], _128_191[12], _128_191[0], _64_127[52], _64_127[40], _64_127[28], _64_127[16], _64_127[4], _0_63[56], _0_63[44], _0_63[32], _0_63[20], _0_63[8], _191_255[61], _191_255[49], _191_255[37], _191_255[25], _191_255[13], _191_255[1], _128_191[53], _128_191[41], _128_191[29], _128_191[17], _128_191[5], _64_127[57], _64_127[45], _64_127[33], _64_127[21], _64_127[9], _0_63[61], _0_63[49], _0_63[37], _0_63[25], _0_63[13], _0_63[1], _191_255[54], _191_255[42], _191_255[30], _191_255[18], _191_255[6], _128_191[58], _128_191[46], _128_191[34], _128_191[22], _128_191[10], _64_127[62], _64_127[50], _64_127[38], _64_127[26], _64_127[14], _64_127[2], _0_63[54], _0_63[42], _0_63[30], _0_63[18], _0_63[6], _191_255[59]};
  assign _256_2 = _191_255[53];
endmodule
