// Digital circuit χ.dig as structural Verilog
// χ : s_i ← s_i + (s_i+1 + 1)s_i+2 ,
module \χ  (
  input  [63:0] _64_127_2,
  input  [63:0] _128_191_2,
  input  [63:0] _191_255,
  input  [63:0] _0_63_2,
  input  _256_2,
  output [63:0] _0_63,
  output [63:0] _64_127,
  output [63:0] _128_191,
  output [63:0] _192_255,
  output _256
);

  x x_1 (.s({_0_63_2[1:0], _256_2}), .o(_256));
  x x_2 (.s({_0_63_2[0], _256_2, _191_255[63]}), .o(_192_255[63]));
  x x_3 (.s({_256_2, _191_255[63:62]}), .o(_192_255[62]));
  x64_61 x64_61_1 (.i_64(_191_255), .o_64(_192_255[61:0]));
  x x_4 (.s({_191_255[1:0], _128_191_2[63]}), .o(_128_191[63]));
  x x_5 (.s({_191_255[0], _128_191_2[63:62]}), .o(_128_191[62]));
  x64_61 x64_61_2 (.i_64(_128_191_2), .o_64(_128_191[61:0]));
  x x_6 (.s({_128_191_2[1:0], _64_127_2[63]}), .o(_64_127[63]));
  x x_7 (.s({_128_191_2[0], _64_127_2[63:62]}), .o(_64_127[62]));
  x64_61 x64_61_3 (.i_64(_64_127_2), .o_64(_64_127[61:0]));
  x x_8 (.s({_64_127_2[1:0], _0_63_2[63]}), .o(_0_63[63]));
  x x_9 (.s({_64_127_2[0], _0_63_2[63:62]}), .o(_0_63[62]));
  x64_61 x64_61_4 (.i_64(_0_63_2), .o_64(_0_63[61:0]));
endmodule
